// Logisim project final.circ as structural Verilog: 28 circuits, main circuit main
module main (
  output [63:0] out_1,
  output [63:0] out_2,
  output [63:0] out_3,
  output [63:0] out_4,
  output [4:0] out_5,
  output [3:0] out_6,
  output [3:0] out_7,
  output [3:0] out_8,
  output [3:0] out_9,
  output [63:0] out_10,
  output [63:0] out_11,
  output [11:0] out_12,
  output [11:0] out_13,
  output [7:0] out_14
);

  wire clock_1_out, cond_1_cnd, enables_1_ena, enables_1_enb, enables_1_ene, enables_1_enm, mem_read_1_read,
       mem_write_1_read, setcc_1_out_3;
  wire [1:0] alu_1_cc, cc_1_cc_out;
  wire [2:0] alufun_1_alu;
  wire [3:0] enables_1_a, enables_1_b;
  wire [11:0] fetch_main_1_valp;
  wire [63:0] data_memory_1_valm, mem_addr_1_data_memory, mem_data_1_data_mem;

  Clock clock_1 (.out(clock_1_out));
  cycle_count cycle_count_1 (.clk(clock_1_out), .count(out_5));
  ROM #(.addrWidth(12)) rom_1 (.addr(out_13), .data(out_14));
  address address_1 (.cycle(out_5), .PC(out_12), .addr(out_13));
  cond cond_1 (.CC(cc_1_cc_out), .cycle(out_5), .clk(clock_1_out), .ifun(out_6), .cnd(cond_1_cnd));
  CC cc_1 (.setCC(setcc_1_out_3), .clk(clock_1_out), .CCfromALU(alu_1_cc), .CC_Out(cc_1_cc_out));
  setCC setcc_1 (.cycle(out_5), .icode(out_8), .out_3(setcc_1_out_3));
  new_PC new_pc_1 (
    .icode(out_8), .cnd(cond_1_cnd), .valM(data_memory_1_valm), .valC(out_11), .valP(fetch_main_1_valp),
    .cycle(out_5), .clk(clock_1_out), .PC(out_12));
  Mem_read mem_read_1 (.icode(out_8), .cycle(out_5), .read(mem_read_1_read));
  Mem_write mem_write_1 (.icode(out_8), .cycle(out_5), .read(mem_write_1_read));
  ALU alu_1 (.ALUA(out_1), .ALUB(out_2), .fromALUfun(alufun_1_alu), .CC(alu_1_cc), .valE(out_10));
  ALUA alua_1 (.icode(out_8), .valA(out_4), .valC(out_11), .ALU(out_1));
  Fetch_Main fetch_main_1 (
    .PC(out_12), .data(out_14), .cycle(out_5), .clk(clock_1_out), .icode(out_8), .ifun(out_6),
    .valP(fetch_main_1_valp), .rA(out_9), .rB(out_7), .valC(out_11));
  Mem_addr mem_addr_1 (.icode(out_8), .valE(out_10), .valA(out_4), .Data_memory(mem_addr_1_data_memory));
  Data_memory data_memory_1 (
    .read(mem_read_1_read), .memaddr(mem_addr_1_data_memory), .clk(clock_1_out), .write(mem_write_1_read),
    .memdata(mem_data_1_data_mem), .cycle_num(out_5), .valM(data_memory_1_valm));
  Mem_data mem_data_1 (.icode(out_8), .valA(out_4), .valP(fetch_main_1_valp), .data_mem(mem_data_1_data_mem));
  ALUfun alufun_1 (.icode(out_8), .ifun(out_6), .ALU(alufun_1_alu));
  ALUB alub_1 (.icode(out_8), .valB(out_3), .ALU(out_2));
  register_file register_file_1 (
    .enB(enables_1_enb), .srcB(enables_1_b), .enA(enables_1_ena), .srcA(enables_1_a), .enE(enables_1_ene),
    .enM(enables_1_enm), .dstE(enables_1_b), .dstM(enables_1_a), .valM(data_memory_1_valm), .valE(out_10),
    .clk(clock_1_out), .valA(out_4), .valB(out_3));
  enables enables_1 (
    .rB(out_7), .cycle(out_5), .icode(out_8), .rA(out_9), .B(enables_1_b), .enE(enables_1_ene),
    .enM(enables_1_enm), .enA(enables_1_ena), .enB(enables_1_enb), .A(enables_1_a));

  // Notes on the sheet:
  //   contents of rom_1 (hex, n*v repeats v):
  //   30 f0 9*11 30 f1 8*22 0 30 f2 8*33 40 9*0 50 30 8*0 61 11 76
endmodule

module new_PC (
  input  clk,
  input  [3:0] icode,
  input  cnd,
  input  [11:0] valP,
  input  [63:0] valM,
  input  [63:0] valC,
  input  [4:0] cycle,
  output [11:0] PC
);

  wire decoder_1_out0, decoder_1_out1, decoder_1_out2, decoder_1_out3, decoder_1_out4, decoder_1_out5,
       decoder_1_out6, decoder_1_out7, decoder_1_out8, decoder_1_out9, decoder_1_out10, decoder_1_out11,
       demultiplexer_1_out0, demultiplexer_1_out1, demultiplexer_2_out18, demultiplexer_2_out19, or_1_out,
       or_2_out;
  wire [11:0] controlled_buffer_1_out;

  Decoder #(.enable("false"), .select(4)) decoder_1 (
    .out0(decoder_1_out0), .out1(decoder_1_out1), .out2(decoder_1_out2), .out3(decoder_1_out3),
    .out4(decoder_1_out4), .out5(decoder_1_out5), .out6(decoder_1_out6), .out7(decoder_1_out7),
    .out8(decoder_1_out8), .out9(decoder_1_out9), .out10(decoder_1_out10), .out11(decoder_1_out11),
    .sel(icode));  // open: out12, out13, out14, out15
  Demultiplexer demultiplexer_1 (
    .out0(demultiplexer_1_out0), .out1(demultiplexer_1_out1), .in(decoder_1_out7), .sel(cnd));
  or or_1 (or_1_out, demultiplexer_1_out1, decoder_1_out8);
  or or_2 (or_2_out, decoder_1_out11, decoder_1_out10, demultiplexer_1_out0, decoder_1_out6, decoder_1_out5, decoder_1_out4, decoder_1_out3, decoder_1_out2, decoder_1_out1, decoder_1_out0);
  assign controlled_buffer_1_out = or_2_out ? valP : 12'bz;  // Controlled_Buffer controlled_buffer_1
  assign controlled_buffer_1_out = decoder_1_out9 ? valM[11:0] : 12'bz;  // Controlled_Buffer controlled_buffer_2
  assign controlled_buffer_1_out = or_1_out ? valC[11:0] : 12'bz;  // Controlled_Buffer controlled_buffer_3
  Demultiplexer #(.select(5)) demultiplexer_2 (
    .out18(demultiplexer_2_out18), .out19(demultiplexer_2_out19), .in(1'b1), .sel(cycle));  // open: out0, out1, out2, out3, out4, out5, out6, out7, out8, out9, out10, out11, out12, out13, out14, out15, out16, out17, out20, out21, out22, out23, out24, out25, out26, out27, out28, out29, out30, out31
  Register #(.width(12)) rsp (.D(controlled_buffer_1_out), .en(demultiplexer_2_out18), .Q(PC), .clk(clk));  // open: clr
endmodule

module register_file (
  input  [63:0] valM,
  input  enA,
  input  [3:0] srcA,
  input  enM,
  input  [3:0] dstM,
  input  [63:0] valE,
  input  clk,
  input  enB,
  input  enE,
  input  [3:0] srcB,
  input  [3:0] dstE,
  output [63:0] valA,
  output [63:0] valB
);

  wire custom_or_1_out_3, custom_or_2_out_3, custom_or_3_out_3, custom_or_4_out_3, custom_or_5_out_3,
       custom_or_6_out_3, custom_or_7_out_3, custom_or_8_out_3, custom_or_9_out_3, custom_or_10_out_3,
       custom_or_11_out_3, custom_or_12_out_3, custom_or_13_out_3, custom_or_14_out_3, custom_or_15_out_3,
       decoder_1_out0, decoder_1_out1, decoder_1_out2, decoder_1_out3, decoder_1_out4, decoder_1_out5,
       decoder_1_out6, decoder_1_out7, decoder_1_out8, decoder_1_out9, decoder_1_out10, decoder_1_out11,
       decoder_1_out12, decoder_1_out13, decoder_1_out14, decoder_2_out0, decoder_2_out1, decoder_2_out2,
       decoder_2_out3, decoder_2_out4, decoder_2_out5, decoder_2_out6, decoder_2_out7, decoder_2_out8,
       decoder_2_out9, decoder_2_out10, decoder_2_out11, decoder_2_out12, decoder_2_out13, decoder_2_out14,
       decoder_3_out0, decoder_3_out1, decoder_3_out2, decoder_3_out3, decoder_3_out4, decoder_3_out5,
       decoder_3_out6, decoder_3_out7, decoder_3_out8, decoder_3_out9, decoder_3_out10, decoder_3_out11,
       decoder_3_out12, decoder_3_out13, decoder_3_out14, decoder_4_out0, decoder_4_out1, decoder_4_out2,
       decoder_4_out3, decoder_4_out4, decoder_4_out5, decoder_4_out6, decoder_4_out7, decoder_4_out8,
       decoder_4_out9, decoder_4_out10, decoder_4_out11, decoder_4_out12, decoder_4_out13, decoder_4_out14;
  wire [63:0] controlled_buffer_1_out, controlled_buffer_3_out, controlled_buffer_5_out,
       controlled_buffer_7_out, controlled_buffer_9_out, controlled_buffer_11_out, controlled_buffer_13_out,
       controlled_buffer_15_out, controlled_buffer_17_out, controlled_buffer_19_out,
       controlled_buffer_21_out, controlled_buffer_23_out, controlled_buffer_25_out,
       controlled_buffer_27_out, controlled_buffer_29_out, r0_q, r1_q, r2_q, r3_q, r4_q, r5_q, r6_q, r7_q,
       r8_q, r9_q, ra_q, rb_q, rc_q, rd_q, re_q;

  Decoder #(.select(4)) decoder_1 (
    .out0(decoder_1_out0), .out1(decoder_1_out1), .out2(decoder_1_out2), .out3(decoder_1_out3),
    .out4(decoder_1_out4), .out5(decoder_1_out5), .out6(decoder_1_out6), .out7(decoder_1_out7),
    .out8(decoder_1_out8), .out9(decoder_1_out9), .out10(decoder_1_out10), .out11(decoder_1_out11),
    .out12(decoder_1_out12), .out13(decoder_1_out13), .out14(decoder_1_out14), .sel(dstM), .en(enM));  // open: out15
  Decoder #(.select(4)) decoder_2 (
    .out0(decoder_2_out0), .out1(decoder_2_out1), .out2(decoder_2_out2), .out3(decoder_2_out3),
    .out4(decoder_2_out4), .out5(decoder_2_out5), .out6(decoder_2_out6), .out7(decoder_2_out7),
    .out8(decoder_2_out8), .out9(decoder_2_out9), .out10(decoder_2_out10), .out11(decoder_2_out11),
    .out12(decoder_2_out12), .out13(decoder_2_out13), .out14(decoder_2_out14), .sel(dstE), .en(enE));  // open: out15
  assign controlled_buffer_1_out = decoder_1_out0 ? valM : 64'bz;  // Controlled_Buffer controlled_buffer_1
  assign controlled_buffer_1_out = decoder_2_out0 ? valE : 64'bz;  // Controlled_Buffer controlled_buffer_2
  assign controlled_buffer_3_out = decoder_1_out1 ? valM : 64'bz;  // Controlled_Buffer controlled_buffer_3
  assign controlled_buffer_3_out = decoder_2_out1 ? valE : 64'bz;  // Controlled_Buffer controlled_buffer_4
  assign controlled_buffer_5_out = decoder_1_out2 ? valM : 64'bz;  // Controlled_Buffer controlled_buffer_5
  assign controlled_buffer_5_out = decoder_2_out2 ? valE : 64'bz;  // Controlled_Buffer controlled_buffer_6
  assign controlled_buffer_7_out = decoder_1_out3 ? valM : 64'bz;  // Controlled_Buffer controlled_buffer_7
  assign controlled_buffer_7_out = decoder_2_out3 ? valE : 64'bz;  // Controlled_Buffer controlled_buffer_8
  assign controlled_buffer_9_out = decoder_1_out4 ? valM : 64'bz;  // Controlled_Buffer controlled_buffer_9
  assign controlled_buffer_9_out = decoder_2_out4 ? valE : 64'bz;  // Controlled_Buffer controlled_buffer_10
  assign controlled_buffer_11_out = decoder_1_out5 ? valM : 64'bz;  // Controlled_Buffer controlled_buffer_11
  assign controlled_buffer_11_out = decoder_2_out5 ? valE : 64'bz;  // Controlled_Buffer controlled_buffer_12
  assign controlled_buffer_13_out = decoder_1_out6 ? valM : 64'bz;  // Controlled_Buffer controlled_buffer_13
  assign controlled_buffer_13_out = decoder_2_out6 ? valE : 64'bz;  // Controlled_Buffer controlled_buffer_14
  assign controlled_buffer_15_out = decoder_1_out7 ? valM : 64'bz;  // Controlled_Buffer controlled_buffer_15
  assign controlled_buffer_15_out = decoder_2_out7 ? valE : 64'bz;  // Controlled_Buffer controlled_buffer_16
  assign controlled_buffer_17_out = decoder_1_out8 ? valM : 64'bz;  // Controlled_Buffer controlled_buffer_17
  assign controlled_buffer_17_out = decoder_2_out8 ? valE : 64'bz;  // Controlled_Buffer controlled_buffer_18
  assign controlled_buffer_19_out = decoder_1_out9 ? valM : 64'bz;  // Controlled_Buffer controlled_buffer_19
  assign controlled_buffer_19_out = decoder_2_out9 ? valE : 64'bz;  // Controlled_Buffer controlled_buffer_20
  assign controlled_buffer_21_out = decoder_1_out10 ? valM : 64'bz;  // Controlled_Buffer controlled_buffer_21
  assign controlled_buffer_21_out = decoder_2_out10 ? valE : 64'bz;  // Controlled_Buffer controlled_buffer_22
  assign controlled_buffer_23_out = decoder_1_out11 ? valM : 64'bz;  // Controlled_Buffer controlled_buffer_23
  assign controlled_buffer_23_out = decoder_2_out11 ? valE : 64'bz;  // Controlled_Buffer controlled_buffer_24
  assign controlled_buffer_25_out = decoder_1_out12 ? valM : 64'bz;  // Controlled_Buffer controlled_buffer_25
  assign controlled_buffer_25_out = decoder_2_out12 ? valE : 64'bz;  // Controlled_Buffer controlled_buffer_26
  assign controlled_buffer_27_out = decoder_1_out13 ? valM : 64'bz;  // Controlled_Buffer controlled_buffer_27
  assign controlled_buffer_27_out = decoder_2_out13 ? valE : 64'bz;  // Controlled_Buffer controlled_buffer_28
  assign controlled_buffer_29_out = decoder_1_out14 ? valM : 64'bz;  // Controlled_Buffer controlled_buffer_29
  assign controlled_buffer_29_out = decoder_2_out14 ? valE : 64'bz;  // Controlled_Buffer controlled_buffer_30
  Register #(.width(64)) r0 (.D(controlled_buffer_1_out), .en(custom_or_1_out_3), .Q(r0_q), .clk(clk));  // open: clr
  custom_or custom_or_1 (.in_2(decoder_1_out0), .in_1(decoder_2_out0), .out_3(custom_or_1_out_3));
  Register #(.width(64)) r1 (.D(controlled_buffer_3_out), .en(custom_or_2_out_3), .Q(r1_q), .clk(clk));  // open: clr
  custom_or custom_or_2 (.in_2(decoder_1_out1), .in_1(decoder_2_out1), .out_3(custom_or_2_out_3));
  Register #(.width(64)) r2 (.D(controlled_buffer_5_out), .en(custom_or_3_out_3), .Q(r2_q), .clk(clk));  // open: clr
  custom_or custom_or_3 (.in_2(decoder_1_out2), .in_1(decoder_2_out2), .out_3(custom_or_3_out_3));
  Register #(.width(64)) r3 (.D(controlled_buffer_7_out), .en(custom_or_4_out_3), .Q(r3_q), .clk(clk));  // open: clr
  custom_or custom_or_4 (.in_2(decoder_1_out3), .in_1(decoder_2_out3), .out_3(custom_or_4_out_3));
  Register #(.width(64)) r4 (.D(controlled_buffer_9_out), .en(custom_or_5_out_3), .Q(r4_q), .clk(clk));  // open: clr
  custom_or custom_or_5 (.in_2(decoder_1_out4), .in_1(decoder_2_out4), .out_3(custom_or_5_out_3));
  Register #(.width(64)) r5 (.D(controlled_buffer_11_out), .en(custom_or_6_out_3), .Q(r5_q), .clk(clk));  // open: clr
  custom_or custom_or_6 (.in_2(decoder_1_out5), .in_1(decoder_2_out5), .out_3(custom_or_6_out_3));
  Register #(.width(64)) r6 (.D(controlled_buffer_13_out), .en(custom_or_7_out_3), .Q(r6_q), .clk(clk));  // open: clr
  custom_or custom_or_7 (.in_2(decoder_1_out6), .in_1(decoder_2_out6), .out_3(custom_or_7_out_3));
  Register #(.width(64)) r7 (.D(controlled_buffer_15_out), .en(custom_or_8_out_3), .Q(r7_q), .clk(clk));  // open: clr
  custom_or custom_or_8 (.in_2(decoder_1_out7), .in_1(decoder_2_out7), .out_3(custom_or_8_out_3));
  Register #(.width(64)) r8 (.D(controlled_buffer_17_out), .en(custom_or_9_out_3), .Q(r8_q), .clk(clk));  // open: clr
  custom_or custom_or_9 (.in_2(decoder_1_out8), .in_1(decoder_2_out8), .out_3(custom_or_9_out_3));
  Register #(.width(64)) r9 (.D(controlled_buffer_19_out), .en(custom_or_10_out_3), .Q(r9_q), .clk(clk));  // open: clr
  custom_or custom_or_10 (.in_2(decoder_1_out9), .in_1(decoder_2_out9), .out_3(custom_or_10_out_3));
  Register #(.width(64)) ra (.D(controlled_buffer_21_out), .en(custom_or_11_out_3), .Q(ra_q), .clk(clk));  // open: clr
  custom_or custom_or_11 (.in_2(decoder_1_out10), .in_1(decoder_2_out10), .out_3(custom_or_11_out_3));
  Register #(.width(64)) rb (.D(controlled_buffer_23_out), .en(custom_or_12_out_3), .Q(rb_q), .clk(clk));  // open: clr
  custom_or custom_or_12 (.in_2(decoder_1_out11), .in_1(decoder_2_out11), .out_3(custom_or_12_out_3));
  Register #(.width(64)) rc (.D(controlled_buffer_25_out), .en(custom_or_13_out_3), .Q(rc_q), .clk(clk));  // open: clr
  custom_or custom_or_13 (.in_2(decoder_1_out12), .in_1(decoder_2_out12), .out_3(custom_or_13_out_3));
  Register #(.width(64)) rd (.D(controlled_buffer_27_out), .en(custom_or_14_out_3), .Q(rd_q), .clk(clk));  // open: clr
  custom_or custom_or_14 (.in_2(decoder_1_out13), .in_1(decoder_2_out13), .out_3(custom_or_14_out_3));
  Register #(.width(64)) re (.D(controlled_buffer_29_out), .en(custom_or_15_out_3), .Q(re_q), .clk(clk));  // open: clr
  custom_or custom_or_15 (.in_2(decoder_1_out14), .in_1(decoder_2_out14), .out_3(custom_or_15_out_3));
  assign valA = decoder_3_out0 ? r0_q : 64'bz;  // Controlled_Buffer controlled_buffer_31
  assign valB = decoder_4_out0 ? r0_q : 64'bz;  // Controlled_Buffer controlled_buffer_32
  assign valA = decoder_3_out1 ? r1_q : 64'bz;  // Controlled_Buffer controlled_buffer_33
  assign valB = decoder_4_out1 ? r1_q : 64'bz;  // Controlled_Buffer controlled_buffer_34
  assign valA = decoder_3_out2 ? r2_q : 64'bz;  // Controlled_Buffer controlled_buffer_35
  assign valB = decoder_4_out2 ? r2_q : 64'bz;  // Controlled_Buffer controlled_buffer_36
  assign valA = decoder_3_out3 ? r3_q : 64'bz;  // Controlled_Buffer controlled_buffer_37
  assign valB = decoder_4_out3 ? r3_q : 64'bz;  // Controlled_Buffer controlled_buffer_38
  assign valA = decoder_3_out4 ? r4_q : 64'bz;  // Controlled_Buffer controlled_buffer_39
  assign valB = decoder_4_out4 ? r4_q : 64'bz;  // Controlled_Buffer controlled_buffer_40
  assign valA = decoder_3_out5 ? r5_q : 64'bz;  // Controlled_Buffer controlled_buffer_41
  assign valB = decoder_4_out5 ? r5_q : 64'bz;  // Controlled_Buffer controlled_buffer_42
  assign valA = decoder_3_out6 ? r6_q : 64'bz;  // Controlled_Buffer controlled_buffer_43
  assign valB = decoder_4_out6 ? r6_q : 64'bz;  // Controlled_Buffer controlled_buffer_44
  assign valA = decoder_3_out7 ? r7_q : 64'bz;  // Controlled_Buffer controlled_buffer_45
  assign valB = decoder_4_out7 ? r7_q : 64'bz;  // Controlled_Buffer controlled_buffer_46
  assign valA = decoder_3_out8 ? r8_q : 64'bz;  // Controlled_Buffer controlled_buffer_47
  assign valB = decoder_4_out8 ? r8_q : 64'bz;  // Controlled_Buffer controlled_buffer_48
  assign valA = decoder_3_out9 ? r9_q : 64'bz;  // Controlled_Buffer controlled_buffer_49
  assign valB = decoder_4_out9 ? r9_q : 64'bz;  // Controlled_Buffer controlled_buffer_50
  assign valA = decoder_3_out10 ? ra_q : 64'bz;  // Controlled_Buffer controlled_buffer_51
  assign valB = decoder_4_out10 ? ra_q : 64'bz;  // Controlled_Buffer controlled_buffer_52
  assign valA = decoder_3_out11 ? rb_q : 64'bz;  // Controlled_Buffer controlled_buffer_53
  assign valB = decoder_4_out11 ? rb_q : 64'bz;  // Controlled_Buffer controlled_buffer_54
  assign valA = decoder_3_out12 ? rc_q : 64'bz;  // Controlled_Buffer controlled_buffer_55
  assign valB = decoder_4_out12 ? rc_q : 64'bz;  // Controlled_Buffer controlled_buffer_56
  assign valA = decoder_3_out13 ? rd_q : 64'bz;  // Controlled_Buffer controlled_buffer_57
  assign valB = decoder_4_out13 ? rd_q : 64'bz;  // Controlled_Buffer controlled_buffer_58
  assign valA = decoder_3_out14 ? re_q : 64'bz;  // Controlled_Buffer controlled_buffer_59
  assign valB = decoder_4_out14 ? re_q : 64'bz;  // Controlled_Buffer controlled_buffer_60
  Decoder #(.select(4)) decoder_3 (
    .out0(decoder_3_out0), .out1(decoder_3_out1), .out2(decoder_3_out2), .out3(decoder_3_out3),
    .out4(decoder_3_out4), .out5(decoder_3_out5), .out6(decoder_3_out6), .out7(decoder_3_out7),
    .out8(decoder_3_out8), .out9(decoder_3_out9), .out10(decoder_3_out10), .out11(decoder_3_out11),
    .out12(decoder_3_out12), .out13(decoder_3_out13), .out14(decoder_3_out14), .sel(srcA), .en(enA));  // open: out15
  Decoder #(.select(4)) decoder_4 (
    .out0(decoder_4_out0), .out1(decoder_4_out1), .out2(decoder_4_out2), .out3(decoder_4_out3),
    .out4(decoder_4_out4), .out5(decoder_4_out5), .out6(decoder_4_out6), .out7(decoder_4_out7),
    .out8(decoder_4_out8), .out9(decoder_4_out9), .out10(decoder_4_out10), .out11(decoder_4_out11),
    .out12(decoder_4_out12), .out13(decoder_4_out13), .out14(decoder_4_out14), .sel(srcB), .en(enB));  // open: out15
endmodule

module custom_or (
  input  in_1,
  input  in_2,
  output out_3
);

  or or_1 (out_3, in_1, in_2);
endmodule

module enables (
  input  [3:0] rA,
  input  [3:0] rB,
  input  [4:0] cycle,
  input  [3:0] icode,
  output [3:0] A,
  output [3:0] B,
  output enE,
  output enM,
  output enA,
  output enB
);

  wire decoder_1_out19, decoder_2_out2, decoder_2_out3, decoder_2_out4, decoder_2_out5, decoder_2_out6,
       decoder_2_out7, decoder_2_out8, decoder_2_out9, decoder_2_out10, decoder_2_out11, not_1_out,
       not_2_out, or_1_out, or_2_out, or_5_out, or_6_out;

  Decoder #(.select(5)) decoder_1 (
    .out19(decoder_1_out19), .sel(cycle), .en(1'b1));  // open: out0, out1, out2, out3, out4, out5, out6, out7, out8, out9, out10, out11, out12, out13, out14, out15, out16, out17, out18, out20, out21, out22, out23, out24, out25, out26, out27, out28, out29, out30, out31
  Decoder #(.select(4)) decoder_2 (
    .out2(decoder_2_out2), .out3(decoder_2_out3), .out4(decoder_2_out4), .out5(decoder_2_out5),
    .out6(decoder_2_out6), .out7(decoder_2_out7), .out8(decoder_2_out8), .out9(decoder_2_out9),
    .out10(decoder_2_out10), .out11(decoder_2_out11), .sel(icode), .en(1'b1));  // open: out0, out1, out12, out13, out14, out15
  and and_1 (enE, or_1_out, decoder_1_out19);
  or or_1 (or_1_out, decoder_2_out2, decoder_2_out3, decoder_2_out6, decoder_2_out8, decoder_2_out9, decoder_2_out10, decoder_2_out11);
  and and_2 (enM, or_2_out, decoder_1_out19);
  or or_2 (or_2_out, decoder_2_out5, decoder_2_out11);
  or or_3 (enA, decoder_2_out2, decoder_2_out4, decoder_2_out6, decoder_2_out9, decoder_2_out10, decoder_2_out11);
  or or_4 (enB, decoder_2_out4, decoder_2_out5, decoder_2_out6, decoder_2_out8, decoder_2_out9, decoder_2_out10, decoder_2_out11);
  assign A = not_1_out ? rA : 4'bz;  // Controlled_Buffer controlled_buffer_1
  assign A = or_5_out ? 4'b0100 : 4'bz;  // Controlled_Buffer controlled_buffer_2
  not not_1 (not_1_out, or_5_out);
  or or_5 (or_5_out, decoder_2_out9, decoder_2_out10, decoder_2_out11);
  assign B = or_6_out ? 4'b0100 : 4'bz;  // Controlled_Buffer controlled_buffer_3
  assign B = not_2_out ? rB : 4'bz;  // Controlled_Buffer controlled_buffer_4
  or or_6 (or_6_out, decoder_2_out8, decoder_2_out9, decoder_2_out10, decoder_2_out11);
  not not_2 (not_2_out, or_6_out);
endmodule

module decode (
  input  [63:0] valM,
  input  [63:0] valE,
  input  clk,
  input  [3:0] rA,
  input  [3:0] rB,
  input  [3:0] icode,
  output [63:0] valA,
  output [63:0] valB
);

  wire enables_1_ena, enables_1_enb, enables_1_ene, enables_1_enm;
  wire [3:0] enables_1_a, enables_1_b;

  register_file register_file_1 (
    .enB(enables_1_enb), .srcB(enables_1_b), .enA(enables_1_ena), .srcA(enables_1_a), .enE(enables_1_ene),
    .enM(enables_1_enm), .dstE(enables_1_b), .dstM(enables_1_a), .valM(valM), .valE(valE), .clk(clk),
    .valA(valA), .valB(valB));
  enables enables_1 (
    .rB(rB), .icode(icode), .rA(rA), .B(enables_1_b), .enE(enables_1_ene), .enM(enables_1_enm),
    .enA(enables_1_ena), .enB(enables_1_enb), .A(enables_1_a));  // open: cycle
endmodule

module ALUA (
  input  [3:0] icode,
  input  [63:0] valC,
  input  [63:0] valA,
  output [63:0] ALU
);

  wire A_out, B_out, et_out, fr_out, fv_out, nin_out, not_1_out, not_2_out, not_3_out, not_4_out, not_5_out,
       not_6_out, not_7_out, not_8_out, not_9_out, not_10_out, not_11_out, not_12_out, not_13_out,
       not_14_out, not_15_out, not_16_out, not_17_out, not_18_out, not_19_out, not_20_out, sx_out, tre_out,
       two_out;
  wire [3:0] too_out, undriven;
  wire [63:0] undriven_2, undriven_3, undriven_4;

  not not_1 (not_1_out, undriven[0]);
  and sx (sx_out, not_1_out, undriven[1], undriven[2], not_2_out);
  not not_2 (not_2_out, undriven[3]);
  not not_3 (not_3_out, undriven[0]);
  and two (two_out, not_3_out, undriven[1], not_4_out, not_5_out);
  not not_4 (not_4_out, undriven[2]);
  not not_5 (not_5_out, undriven[3]);
  and tre (tre_out, undriven[0], undriven[1], not_6_out, not_7_out);
  not not_6 (not_6_out, undriven[2]);
  not not_7 (not_7_out, undriven[3]);
  not not_8 (not_8_out, undriven[0]);
  not not_9 (not_9_out, undriven[1]);
  and fr (fr_out, not_8_out, not_9_out, undriven[2], not_10_out);
  not not_10 (not_10_out, undriven[3]);
  not not_11 (not_11_out, undriven[1]);
  and fv (fv_out, undriven[0], not_11_out, undriven[2], not_12_out);
  not not_12 (not_12_out, undriven[3]);
  not not_13 (not_13_out, undriven[0]);
  not not_14 (not_14_out, undriven[1]);
  and et (et_out, not_13_out, not_14_out, not_15_out, undriven[3]);
  not not_15 (not_15_out, undriven[2]);
  not not_16 (not_16_out, undriven[1]);
  and nin (nin_out, undriven[0], not_16_out, not_17_out, undriven[3]);
  not not_17 (not_17_out, undriven[2]);
  not not_18 (not_18_out, undriven[0]);
  and A (A_out, not_18_out, undriven[1], not_19_out, undriven[3]);
  not not_19 (not_19_out, undriven[2]);
  and B (B_out, undriven[0], undriven[1], not_20_out, undriven[3]);
  not not_20 (not_20_out, undriven[2]);
  or too (too_out[0], sx_out, two_out);
  or one (too_out[1], tre_out, fr_out, fv_out);
  or three (too_out[2], et_out, A_out);
  or four (too_out[3], nin_out, B_out);
  Multiplexer #(.select(4), .width(64)) multiplexer_1 (
    .in2(valA), .in3(valC), .in4(valC), .in5(valC), .in6(valA), .in8(64'h8), .in9(64'h8), .in10(64'h8),
    .in11(64'h8), .out(ALU), .sel(icode));  // open: in0, in1, in7, in12, in13, in14, in15
  Multiplexer #(.select(4), .width(64)) multiplexer_2 (
    .in1(undriven_2), .in2(undriven_3), .in4(undriven_4), .in8(64'h8), .sel(too_out));  // open: in0, in3, in5, in6, in7, in9, in10, in11, in12, in13, in14, in15, out
endmodule

module ALUB (
  input  [63:0] valB,
  input  [3:0] icode,
  output [63:0] ALU
);

  wire A_out, B_out, et_out, fr_out, fv_out, nin_out, not_1_out, not_2_out, not_3_out, not_4_out, not_5_out,
       not_6_out, not_7_out, not_8_out, not_9_out, not_10_out, not_11_out, not_12_out, not_13_out,
       not_14_out, not_15_out, not_16_out, not_17_out, not_18_out, not_19_out, not_20_out, sx_out, tre_out;
  wire [1:0] two_out;

  not not_1 (not_1_out, icode[0]);
  and sx (sx_out, not_1_out, icode[1], icode[2], not_2_out);
  not not_2 (not_2_out, icode[3]);
  not not_3 (not_3_out, icode[0]);
  and two (two_out[0], not_3_out, icode[1], not_4_out, not_5_out);
  not not_4 (not_4_out, icode[2]);
  not not_5 (not_5_out, icode[3]);
  and tre (tre_out, icode[0], icode[1], not_6_out, not_7_out);
  not not_6 (not_6_out, icode[2]);
  not not_7 (not_7_out, icode[3]);
  not not_8 (not_8_out, icode[0]);
  not not_9 (not_9_out, icode[1]);
  and fr (fr_out, not_8_out, not_9_out, icode[2], not_10_out);
  not not_10 (not_10_out, icode[3]);
  not not_11 (not_11_out, icode[1]);
  and fv (fv_out, icode[0], not_11_out, icode[2], not_12_out);
  not not_12 (not_12_out, icode[3]);
  not not_13 (not_13_out, icode[0]);
  not not_14 (not_14_out, icode[1]);
  and et (et_out, not_13_out, not_14_out, not_15_out, icode[3]);
  not not_15 (not_15_out, icode[2]);
  not not_16 (not_16_out, icode[1]);
  and nin (nin_out, icode[0], not_16_out, not_17_out, icode[3]);
  not not_17 (not_17_out, icode[2]);
  not not_18 (not_18_out, icode[0]);
  and A (A_out, not_18_out, icode[1], not_19_out, icode[3]);
  not not_19 (not_19_out, icode[2]);
  and B (B_out, icode[0], icode[1], not_20_out, icode[3]);
  not not_20 (not_20_out, icode[2]);
  or or_1 (two_out[1], sx_out, tre_out, fr_out, fv_out, et_out, nin_out, A_out, B_out);
  Multiplexer #(.select(2), .width(64)) multiplexer_1 (
    .in1({64{1'b0}}), .in2(valB), .out(ALU), .sel(two_out));  // open: in0, in3
endmodule

module ALU (
  input  [2:0] fromALUfun,
  input  [63:0] ALUA,
  input  [63:0] ALUB,
  output [63:0] valE,
  output [1:0] CC
);

  wire iszero_1_out_2;
  wire [0:0] adder_1_cout;
  wire [1:0] multiplexer_1_out, multiplexer_2_out;
  wire [1:1] subtractor_1_bout;
  wire [63:0] adder_1_out, and_1_out, subtractor_1_out, xor_1_out;

  assign CC = multiplexer_2_out | multiplexer_1_out;  // OR_Gate or_1, 2 bits wide
  Multiplexer #(.select(3), .width(2)) multiplexer_1 (
    .in4({1'b0, adder_1_cout[0]}), .in5({subtractor_1_bout[1], 1'b0}), .in6(2'b00), .in7(2'b00),
    .out(multiplexer_1_out), .sel(fromALUfun));  // open: in0, in1, in2, in3
  Multiplexer #(.width(2)) multiplexer_2 (.in0(2'b00), .in1(2'b11), .out(multiplexer_2_out), .sel(iszero_1_out_2));
  IsZero iszero_1 (.in_1(valE), .out_2(iszero_1_out_2));
  assign xor_1_out = ALUB ^ ALUA;  // XOR_Gate xor_1, 64 bits wide
  assign and_1_out = ALUB & ALUA;  // AND_Gate and_1, 64 bits wide
  Subtractor #(.width(64)) subtractor_1 (
    .a(ALUB), .b(ALUA), .out(subtractor_1_out), .bout(subtractor_1_bout[1]));  // open: bin
  Adder #(.width(64)) adder_1 (.a(ALUB), .b(ALUA), .out(adder_1_out), .cout(adder_1_cout[0]));  // open: cin
  Multiplexer #(.select(3), .width(64)) multiplexer_3 (
    .in4(adder_1_out), .in5(subtractor_1_out), .in6(and_1_out), .in7(xor_1_out), .out(valE), .sel(fromALUfun));  // open: in0, in1, in2, in3

  // Notes on the sheet:
  //   ZF = 11
  //   SF = 10
  //   OF = 01
  //   NO FLAG = 00
  //   001 = ADD
  //   011 = SUB
  //   101 = AND
  //   111 = XOR
endmodule

module ALUfun (
  input  [3:0] ifun,
  input  [3:0] icode,
  output [2:0] ALU
);

  wire A_out, ADD_out, and_1_out, and_2_out, ANDF_out, B_out, eight_out, five_out, four_out, funz_out,
       nine_out, not_1_out, not_2_out, not_3_out, not_4_out, not_5_out, not_6_out, not_7_out, not_8_out,
       not_9_out, not_10_out, not_11_out, not_12_out, not_13_out, not_14_out, not_15_out, not_16_out,
       not_17_out, not_18_out, not_19_out, not_20_out, not_21_out, not_22_out, not_23_out, not_24_out,
       not_25_out, not_26_out, not_27_out, not_28_out, not_29_out, not_30_out, not_31_out, not_32_out,
       onef_out, or_1_out, or_2_out, or_4_out, six_out, SUB_out, threex_out, tre_out, two_out, twoa_out,
       XORF_out;
  wire [2:0] multiplexer_1_out, multiplexer_2_out, multiplexer_3_out, multiplexer_4_out;

  and two (two_out, not_1_out, icode[1], not_2_out, not_7_out);
  not not_1 (not_1_out, icode[0]);
  not not_2 (not_2_out, icode[2]);
  and tre (tre_out, icode[0], icode[1], not_3_out, not_4_out);
  not not_3 (not_3_out, icode[2]);
  not not_4 (not_4_out, icode[3]);
  not not_5 (not_5_out, icode[0]);
  not not_6 (not_6_out, icode[1]);
  not not_7 (not_7_out, icode[3]);
  or or_1 (or_1_out, two_out, tre_out, four_out, five_out, nine_out, B_out);
  and four (four_out, not_5_out, not_6_out, icode[2], not_8_out);
  and five (five_out, icode[0], not_9_out, icode[2], not_10_out);
  not not_8 (not_8_out, icode[3]);
  not not_9 (not_9_out, icode[1]);
  not not_10 (not_10_out, icode[3]);
  Multiplexer #(.width(3)) multiplexer_1 (.in0(3'b000), .in1(3'b100), .out(multiplexer_1_out), .sel(ADD_out));
  and ADD (ADD_out, or_2_out, funz_out);
  or or_2 (or_2_out, or_1_out, six_out);
  and nine (nine_out, icode[0], not_11_out, not_12_out, icode[3]);
  and B (B_out, icode[0], icode[1], not_13_out, icode[3]);
  not not_11 (not_11_out, icode[1]);
  not not_12 (not_12_out, icode[2]);
  and eight (eight_out, not_14_out, not_15_out, not_16_out, icode[3]);
  not not_13 (not_13_out, icode[2]);
  not not_14 (not_14_out, icode[0]);
  not not_15 (not_15_out, icode[1]);
  not not_16 (not_16_out, icode[2]);
  assign ALU = multiplexer_1_out | multiplexer_2_out | multiplexer_3_out | multiplexer_4_out;  // OR_Gate or_3, 3 bits wide
  and and_1 (and_1_out, or_4_out, funz_out);
  or or_4 (or_4_out, eight_out, A_out);
  and A (A_out, not_17_out, icode[2], not_18_out, icode[3]);
  not not_17 (not_17_out, icode[0]);
  not not_18 (not_18_out, icode[2]);
  Multiplexer #(.width(3)) multiplexer_2 (.in0(3'b000), .in1(3'b101), .out(multiplexer_2_out), .sel(SUB_out));
  or SUB (SUB_out, and_1_out, and_2_out);
  and six (six_out, not_19_out, icode[1], icode[2], not_20_out);
  not not_19 (not_19_out, icode[0]);
  not not_20 (not_20_out, icode[3]);
  Multiplexer #(.width(3)) multiplexer_3 (.in0(3'b000), .in1(3'b110), .out(multiplexer_3_out), .sel(ANDF_out));
  and and_2 (and_2_out, six_out, onef_out);
  and ANDF (ANDF_out, six_out, twoa_out);
  and funz (funz_out, not_21_out, not_22_out, not_23_out, not_24_out);
  not not_21 (not_21_out, ifun[0]);
  not not_22 (not_22_out, ifun[1]);
  not not_23 (not_23_out, ifun[2]);
  and onef (onef_out, ifun[0], not_25_out, not_26_out, not_27_out);
  not not_24 (not_24_out, ifun[3]);
  not not_25 (not_25_out, ifun[1]);
  not not_26 (not_26_out, ifun[2]);
  not not_27 (not_27_out, ifun[3]);
  Multiplexer #(.width(3)) multiplexer_4 (.in0(3'b000), .in1(3'b111), .out(multiplexer_4_out), .sel(XORF_out));
  and XORF (XORF_out, six_out, threex_out);
  and twoa (twoa_out, not_28_out, ifun[1], not_29_out, not_30_out);
  not not_28 (not_28_out, ifun[0]);
  not not_29 (not_29_out, ifun[2]);
  not not_30 (not_30_out, ifun[3]);
  and threex (threex_out, ifun[0], ifun[1], not_31_out, not_32_out);
  not not_31 (not_31_out, ifun[2]);
  not not_32 (not_32_out, ifun[3]);

  // Notes on the sheet:
  //   ADD = 20, 30, 40, 50, 60, 90, B0
  //   SUB = 61, 80, A0
  //   AND = 62
  //   XORL = 63
  //   4 = ADD
  //   5 = SUB
  //   6 = AND
  //   7 = XOR
endmodule

module CC (
  input  [1:0] CCfromALU,
  input  setCC,
  input  clk,
  output [1:0] CC_Out
);

  Register #(.width(2)) register_1 (.D(CCfromALU), .en(setCC), .Q(CC_Out), .clk(clk));  // open: clr

  // Notes on the sheet:
  //   ZF = 11
  //   SF = 10
  //   OF = 01
  //   NO FLAG = 00
endmodule

module cond (
  input  [1:0] CC,
  input  clk,
  input  [3:0] ifun,
  input  [4:0] cycle,
  output cnd
);

  wire and_1_out, ConMet_out, decoder_1_out10, five_out, four_out, jeANDcmove_out, jgANDcmovg_out,
       jgeANDcmovge_out, jlANDcmovl_out, jleANDcmovle_out, jneANDcmovne_out, not_1_out, not_2_out, not_3_out,
       not_4_out, not_5_out, not_6_out, not_7_out, not_8_out, not_9_out, not_10_out, not_11_out, not_12_out,
       not_13_out, not_14_out, not_15_out, not_16_out, not_17_out, not_18_out, not_19_out, not_20_out,
       not_21_out, not_22_out, not_23_out, one_out, or_1_out, OverF_out, SF_out, six_out, three_out, two_out,
       xor_1_out, zero_out, ZF_out;

  not not_1 (not_1_out, CC[1]);
  and ZF (ZF_out, CC[0], CC[1]);
  not not_2 (not_2_out, CC[0]);
  and SF (SF_out, not_2_out, CC[1]);
  and OverF (OverF_out, CC[0], not_1_out);
  and zero (zero_out, not_3_out, not_4_out, not_5_out, not_6_out);
  not not_3 (not_3_out, ifun[0]);
  not not_4 (not_4_out, ifun[1]);
  not not_5 (not_5_out, ifun[2]);
  not not_6 (not_6_out, ifun[3]);
  not not_7 (not_7_out, ZF_out);
  xor xor_1 (xor_1_out, SF_out, OverF_out);
  and one (one_out, ifun[0], not_8_out, not_9_out, not_10_out);
  not not_8 (not_8_out, ifun[1]);
  not not_9 (not_9_out, ifun[2]);
  not not_10 (not_10_out, ifun[3]);
  not not_11 (not_11_out, xor_1_out);
  or or_1 (or_1_out, xor_1_out, ZF_out);
  and two (two_out, not_12_out, ifun[1], not_13_out, not_14_out);
  not not_12 (not_12_out, ifun[0]);
  not not_13 (not_13_out, ifun[2]);
  and and_1 (and_1_out, not_11_out, not_7_out);
  not not_14 (not_14_out, ifun[3]);
  and jeANDcmove (jeANDcmove_out, ZF_out, three_out);
  and three (three_out, ifun[0], ifun[1], not_15_out, not_16_out);
  not not_15 (not_15_out, ifun[2]);
  not not_16 (not_16_out, ifun[3]);
  and four (four_out, not_17_out, not_18_out, ifun[2], not_19_out);
  not not_17 (not_17_out, ifun[0]);
  not not_18 (not_18_out, ifun[1]);
  not not_19 (not_19_out, ifun[3]);
  and jneANDcmovne (jneANDcmovne_out, not_7_out, four_out);
  and jgANDcmovg (jgANDcmovg_out, and_1_out, six_out);
  and five (five_out, ifun[0], not_21_out, ifun[2], not_20_out);
  not not_20 (not_20_out, ifun[3]);
  not not_21 (not_21_out, ifun[1]);
  and jgeANDcmovge (jgeANDcmovge_out, not_11_out, five_out);
  and jlANDcmovl (jlANDcmovl_out, xor_1_out, two_out);
  and jleANDcmovle (jleANDcmovle_out, or_1_out, one_out);
  and six (six_out, not_22_out, ifun[1], ifun[2], not_23_out);
  not not_22 (not_22_out, ifun[0]);
  not not_23 (not_23_out, ifun[3]);
  Decoder #(.enable("false"), .select(5)) decoder_1 (
    .out10(decoder_1_out10), .sel(cycle));  // open: out0, out1, out2, out3, out4, out5, out6, out7, out8, out9, out11, out12, out13, out14, out15, out16, out17, out18, out19, out20, out21, out22, out23, out24, out25, out26, out27, out28, out29, out30, out31
  or ConMet (ConMet_out, jeANDcmove_out, jneANDcmovne_out, jgANDcmovg_out, zero_out, jgeANDcmovge_out, jlANDcmovl_out, jleANDcmovle_out);
  Register #(.width(1)) register_1 (.D(ConMet_out), .en(decoder_1_out10), .Q(cnd), .clk(clk));  // open: clr

  // Notes on the sheet:
  //   ZF = 11
  //   SF = 10
  //   OF = 01
  //   NO FLAG = 00
  //   cmove 3, cmovne 4, cmovg 6, cmovge 5, cmovl 2, cmovle 1
  //   jmp 0, jle 1, jl 2, je 3, jne 4, jge5, jg 6
endmodule

module IsZero (
  input  [63:0] in_1,
  output out_2
);

  wire or_1_out, or_2_out, or_3_out, or_4_out, or_5_out, or_6_out, or_7_out, or_8_out, or_9_out, or_10_out,
       or_11_out, or_12_out, or_13_out, or_14_out, or_15_out, or_16_out, or_17_out, or_18_out, or_19_out,
       or_20_out, or_21_out, or_22_out, or_23_out, or_24_out, or_25_out, or_26_out, or_27_out, or_28_out,
       or_29_out, or_30_out, or_31_out, or_32_out, or_33_out, or_34_out, or_35_out, or_36_out, or_37_out,
       or_38_out, or_39_out, or_40_out, or_41_out, or_42_out, or_43_out, or_44_out, or_45_out, or_46_out,
       or_47_out, or_48_out, or_49_out, or_50_out, or_51_out, or_52_out, or_53_out, or_54_out, or_55_out,
       or_56_out, or_57_out, or_58_out, or_59_out, or_60_out, or_61_out, or_62_out, or_63_out;

  or or_1 (or_1_out, or_2_out, or_4_out);
  not not_1 (out_2, or_1_out);
  or or_2 (or_2_out, or_37_out, or_10_out);
  or or_3 (or_3_out, or_12_out, or_6_out);
  or or_4 (or_4_out, or_3_out, or_9_out);
  or or_5 (or_5_out, or_15_out, or_16_out);
  or or_6 (or_6_out, or_5_out, or_7_out);
  or or_7 (or_7_out, or_17_out, or_18_out);
  or or_8 (or_8_out, or_20_out, or_22_out);
  or or_9 (or_9_out, or_8_out, or_23_out);
  or or_10 (or_10_out, or_39_out, or_25_out);
  or or_11 (or_11_out, or_28_out, or_29_out);
  or or_12 (or_12_out, or_11_out, or_13_out);
  or or_13 (or_13_out, or_30_out, or_14_out);
  or or_14 (or_14_out, in_1[38], in_1[39]);
  or or_15 (or_15_out, in_1[40], in_1[41]);
  or or_16 (or_16_out, in_1[42], in_1[43]);
  or or_17 (or_17_out, in_1[44], in_1[45]);
  or or_18 (or_18_out, in_1[46], in_1[47]);
  or or_19 (or_19_out, in_1[48], in_1[49]);
  or or_20 (or_20_out, or_19_out, or_21_out);
  or or_21 (or_21_out, in_1[50], in_1[51]);
  or or_22 (or_22_out, or_31_out, or_32_out);
  or or_23 (or_23_out, or_34_out, or_36_out);
  or or_24 (or_24_out, or_42_out, or_43_out);
  or or_25 (or_25_out, or_24_out, or_26_out);
  or or_26 (or_26_out, or_44_out, or_27_out);
  or or_27 (or_27_out, in_1[30], in_1[31]);
  or or_28 (or_28_out, in_1[32], in_1[33]);
  or or_29 (or_29_out, in_1[34], in_1[35]);
  or or_30 (or_30_out, in_1[36], in_1[37]);
  or or_31 (or_31_out, in_1[52], in_1[53]);
  or or_32 (or_32_out, in_1[54], in_1[55]);
  or or_33 (or_33_out, in_1[56], in_1[57]);
  or or_34 (or_34_out, or_33_out, or_35_out);
  or or_35 (or_35_out, in_1[58], in_1[59]);
  or or_36 (or_36_out, or_45_out, or_46_out);
  or or_37 (or_37_out, or_55_out, or_48_out);
  or or_38 (or_38_out, or_51_out, or_52_out);
  or or_39 (or_39_out, or_38_out, or_40_out);
  or or_40 (or_40_out, or_53_out, or_41_out);
  or or_41 (or_41_out, in_1[22], in_1[23]);
  or or_42 (or_42_out, in_1[24], in_1[25]);
  or or_43 (or_43_out, in_1[26], in_1[27]);
  or or_44 (or_44_out, in_1[28], in_1[29]);
  or or_45 (or_45_out, in_1[60], in_1[61]);
  or or_46 (or_46_out, in_1[62], in_1[63]);
  or or_47 (or_47_out, or_58_out, or_59_out);
  or or_48 (or_48_out, or_47_out, or_49_out);
  or or_49 (or_49_out, or_60_out, or_50_out);
  or or_50 (or_50_out, in_1[14], in_1[15]);
  or or_51 (or_51_out, in_1[16], in_1[17]);
  or or_52 (or_52_out, in_1[18], in_1[19]);
  or or_53 (or_53_out, in_1[20], in_1[21]);
  or or_54 (or_54_out, or_61_out, or_62_out);
  or or_55 (or_55_out, or_54_out, or_56_out);
  or or_56 (or_56_out, or_63_out, or_57_out);
  or or_57 (or_57_out, in_1[6], in_1[7]);
  or or_58 (or_58_out, in_1[8], in_1[9]);
  or or_59 (or_59_out, in_1[10], in_1[11]);
  or or_60 (or_60_out, in_1[12], in_1[13]);
  or or_61 (or_61_out, in_1[0], in_1[1]);
  or or_62 (or_62_out, in_1[2], in_1[3]);
  or or_63 (or_63_out, in_1[4], in_1[5]);
endmodule

module setCC (
  input  [4:0] cycle,
  input  [3:0] icode,
  output out_3
);

  wire and_2_out, decoder_1_out9, not_1_out, not_2_out;

  Decoder #(.enable("false"), .select(5)) decoder_1 (
    .out9(decoder_1_out9), .out10(decoder_1_out9), .out11(decoder_1_out9), .out12(decoder_1_out9),
    .out13(decoder_1_out9), .out14(decoder_1_out9), .out15(decoder_1_out9), .out16(decoder_1_out9),
    .out17(decoder_1_out9), .out18(decoder_1_out9), .out19(decoder_1_out9), .out20(decoder_1_out9),
    .out21(decoder_1_out9), .out22(decoder_1_out9), .out23(decoder_1_out9), .sel(cycle));  // open: out0, out1, out2, out3, out4, out5, out6, out7, out8, out24, out25, out26, out27, out28, out29, out30, out31
  and and_1 (out_3, decoder_1_out9, and_2_out);
  and and_2 (and_2_out, not_1_out, icode[2], icode[1], not_2_out);
  not not_1 (not_1_out, icode[3]);
  not not_2 (not_2_out, icode[0]);

  // Notes on the sheet:
  //   else set to 0
  //   If icode == 6 (OPq) set to enable (1)
  //   6 (OPq)
endmodule

module execute (
  input  [63:0] valC,
  input  [63:0] valA,
  input  [63:0] valB,
  input  [3:0] icode,
  input  [3:0] ifun,
  output cnd,
  output [63:0] valE,
  output [2:0] out_8,
  output [63:0] out_9,
  output [63:0] out_10
);

  wire setcc_1_p1;
  wire [1:0] alu_1_cc, cc_1_cc_out;

  cond cond_1 (.CC(cc_1_cc_out), .ifun(ifun), .cnd(cnd));  // open: cycle, clk
  CC cc_1 (.setCC(setcc_1_p1), .CCfromALU(alu_1_cc), .CC_Out(cc_1_cc_out));  // open: clk
  // setCC setcc_1: pin names not known; wires that end beside it: setcc_1_p1, icode
  ALU alu_1 (.ALUA(out_9), .ALUB(out_10), .fromALUfun(out_8), .CC(alu_1_cc), .valE(valE));
  ALUA alua_1 (.icode(icode), .valA(valA), .valC(valC), .ALU(out_9));
  ALUB alub_1 (.icode(icode), .valB(valB), .ALU(out_10));
  ALUfun alufun_1 (.icode(icode), .ifun(ifun), .ALU(out_8));
endmodule

module Fetch_Main (
  input  [7:0] data,
  input  [4:0] cycle,
  input  clk,
  input  [11:0] PC,
  output [3:0] icode,
  output [3:0] ifun,
  output [3:0] rA,
  output [3:0] rB,
  output [63:0] valC,
  output [11:0] valP
);

  wire multiplexer_2_out;
  wire [7:0] read_1_byte_1, read_1_byte_2, read_1_byte_3, read_1_byte_4, read_1_byte_5, read_1_byte_6,
       read_1_byte_7, read_1_byte_8, read_1_byte_9;
  wire [11:0] adder_1_out, multiplexer_1_out;

  read read_1 (
    .ReadByte(data), .cycle_count(cycle), .clock(clk), .byte_0({icode, ifun}), .byte_1(read_1_byte_1),
    .byte_2(read_1_byte_2), .byte_3(read_1_byte_3), .byte_4(read_1_byte_4), .byte_5(read_1_byte_5),
    .byte_6(read_1_byte_6), .byte_7(read_1_byte_7), .byte_8(read_1_byte_8), .byte_9(read_1_byte_9));
  Multiplexer #(.select(4), .width(12)) multiplexer_1 (
    .in0(12'h1), .in1(12'h1), .in2(12'h2), .in3(12'ha), .in4(12'ha), .in5(12'ha), .in6(12'h2), .in7(12'h9),
    .in8(12'h9), .in9(12'h1), .in10(12'h9), .in11(12'h2), .out(multiplexer_1_out), .sel(icode));  // open: in12, in13, in14, in15
  Multiplexer #(.select(4)) multiplexer_2 (
    .in0(1'b0), .in1(1'b1), .in2(1'b1), .in3(1'b1), .in4(1'b1), .in5(1'b1), .in6(1'b1), .in7(1'b0),
    .in8(1'b0), .in9(1'b1), .in10(1'b1), .in11(1'b0), .in12(1'b0), .in13(1'b0), .in14(1'b0), .in15(1'b0),
    .out(multiplexer_2_out), .sel(icode));
  Align align_1 (
    .NeedRegis(multiplexer_2_out), .B1(read_1_byte_1), .B2(read_1_byte_2), .B3(read_1_byte_3),
    .B4(read_1_byte_4), .B5(read_1_byte_5), .B6(read_1_byte_6), .B7(read_1_byte_7), .B8(read_1_byte_8),
    .B9(read_1_byte_9), .rA(rA), .rB(rB), .Valc(valC));
  Adder #(.width(12)) adder_1 (.a(multiplexer_1_out), .b(PC), .out(adder_1_out));  // open: cin, cout
  Register #(.width(12)) register_1 (.D(adder_1_out), .en(1'b1), .Q(valP), .clk(clk));  // open: clr
endmodule

module Align (
  input  NeedRegis,
  input  [7:0] B1,
  input  [7:0] B2,
  input  [7:0] B3,
  input  [7:0] B4,
  input  [7:0] B5,
  input  [7:0] B6,
  input  [7:0] B7,
  input  [7:0] B8,
  input  [7:0] B9,
  output [3:0] rA,
  output [3:0] rB,
  output [63:0] Valc
);

  wire not_1_out;

  assign {rA, rB} = NeedRegis ? B1 : 8'bz;  // Controlled_Buffer controlled_buffer_1
  not not_1 (not_1_out, NeedRegis);
  assign Valc = NeedRegis ? {B9, B8, B7, B6, B5, B4, B3, B2} : 64'bz;  // Controlled_Buffer controlled_buffer_2
  assign Valc = not_1_out ? {B1, B2, B3, B4, B5, B6, B7, B8} : 64'bz;  // Controlled_Buffer controlled_buffer_3
endmodule

module CycleCount (
  input  [11:0] address_in,
  input  clk,
  output [11:0] address_out,
  output [4:0] count_out
);

  wire comparator_1_lt, not_1_out;
  wire [11:0] adder_1_out, bit_extender_1_out;

  Counter #(.max('h13), .width(5)) counter_1 (.clk(clk), .Q(count_out));  // open: clr, load, up, count, D, carry
  assign bit_extender_1_out = {{7{1'b0}}, count_out};  // Bit_Extender bit_extender_1
  Adder #(.width(12)) adder_1 (.a(address_in), .b(bit_extender_1_out), .out(adder_1_out));  // open: cin, cout
  Comparator #(.width(12)) comparator_1 (.a(adder_1_out), .b(12'h9), .lt(comparator_1_lt));  // open: gt, eq
  assign address_out = comparator_1_lt ? adder_1_out : 12'bz;  // Controlled_Buffer controlled_buffer_1
  not not_1 (not_1_out, comparator_1_lt);
  assign address_out = not_1_out ? 12'h9 : 12'bz;  // Controlled_Buffer controlled_buffer_2
endmodule

module read (
  input  [7:0] ReadByte,
  input  [4:0] cycle_count,
  input  clock,
  output [7:0] byte_0,
  output [7:0] byte_1,
  output [7:0] byte_2,
  output [7:0] byte_3,
  output [7:0] byte_4,
  output [7:0] byte_5,
  output [7:0] byte_6,
  output [7:0] byte_7,
  output [7:0] byte_8,
  output [7:0] byte_9
);

  wire demultiplexer_1_out0, demultiplexer_1_out1, demultiplexer_1_out2, demultiplexer_1_out3,
       demultiplexer_1_out4, demultiplexer_1_out5, demultiplexer_1_out6, demultiplexer_1_out7,
       demultiplexer_1_out8, demultiplexer_1_out9;
  wire [7:0] controlled_buffer_1_out, controlled_buffer_2_out, controlled_buffer_3_out,
       controlled_buffer_4_out, controlled_buffer_5_out, controlled_buffer_6_out, controlled_buffer_7_out,
       controlled_buffer_8_out, controlled_buffer_9_out, controlled_buffer_10_out;

  Demultiplexer #(.select(5)) demultiplexer_1 (
    .out0(demultiplexer_1_out0), .out1(demultiplexer_1_out1), .out2(demultiplexer_1_out2),
    .out3(demultiplexer_1_out3), .out4(demultiplexer_1_out4), .out5(demultiplexer_1_out5),
    .out6(demultiplexer_1_out6), .out7(demultiplexer_1_out7), .out8(demultiplexer_1_out8),
    .out9(demultiplexer_1_out9), .in(1'b1), .sel(cycle_count));  // open: out10, out11, out12, out13, out14, out15, out16, out17, out18, out19, out20, out21, out22, out23, out24, out25, out26, out27, out28, out29, out30, out31
  assign controlled_buffer_1_out = demultiplexer_1_out0 ? ReadByte : 8'bz;  // Controlled_Buffer controlled_buffer_1
  assign controlled_buffer_2_out = demultiplexer_1_out1 ? ReadByte : 8'bz;  // Controlled_Buffer controlled_buffer_2
  assign controlled_buffer_3_out = demultiplexer_1_out2 ? ReadByte : 8'bz;  // Controlled_Buffer controlled_buffer_3
  assign controlled_buffer_4_out = demultiplexer_1_out3 ? ReadByte : 8'bz;  // Controlled_Buffer controlled_buffer_4
  assign controlled_buffer_5_out = demultiplexer_1_out4 ? ReadByte : 8'bz;  // Controlled_Buffer controlled_buffer_5
  assign controlled_buffer_6_out = demultiplexer_1_out5 ? ReadByte : 8'bz;  // Controlled_Buffer controlled_buffer_6
  assign controlled_buffer_7_out = demultiplexer_1_out6 ? ReadByte : 8'bz;  // Controlled_Buffer controlled_buffer_7
  assign controlled_buffer_8_out = demultiplexer_1_out7 ? ReadByte : 8'bz;  // Controlled_Buffer controlled_buffer_8
  assign controlled_buffer_9_out = demultiplexer_1_out8 ? ReadByte : 8'bz;  // Controlled_Buffer controlled_buffer_9
  assign controlled_buffer_10_out = demultiplexer_1_out9 ? ReadByte : 8'bz;  // Controlled_Buffer controlled_buffer_10
  Register register_1 (.D(controlled_buffer_1_out), .en(demultiplexer_1_out0), .Q(byte_0), .clk(clock));  // open: clr
  Register register_2 (.D(controlled_buffer_2_out), .en(demultiplexer_1_out1), .Q(byte_1), .clk(clock));  // open: clr
  Register register_3 (.D(controlled_buffer_3_out), .en(demultiplexer_1_out2), .Q(byte_2), .clk(clock));  // open: clr
  Register register_4 (.D(controlled_buffer_4_out), .en(demultiplexer_1_out3), .Q(byte_3), .clk(clock));  // open: clr
  Register register_5 (.D(controlled_buffer_5_out), .en(demultiplexer_1_out4), .Q(byte_4), .clk(clock));  // open: clr
  Register register_6 (.D(controlled_buffer_6_out), .en(demultiplexer_1_out5), .Q(byte_5), .clk(clock));  // open: clr
  Register register_7 (.D(controlled_buffer_7_out), .en(demultiplexer_1_out6), .Q(byte_6), .clk(clock));  // open: clr
  Register register_8 (.D(controlled_buffer_8_out), .en(demultiplexer_1_out7), .Q(byte_7), .clk(clock));  // open: clr
  Register register_9 (.D(controlled_buffer_9_out), .en(demultiplexer_1_out8), .Q(byte_8), .clk(clock));  // open: clr
  Register register_10 (.D(controlled_buffer_10_out), .en(demultiplexer_1_out9), .Q(byte_9), .clk(clock));  // open: clr
endmodule

module Mem_addr (
  input  [63:0] valE,
  input  [63:0] valA,
  input  [3:0] icode,
  output [63:0] Data_memory
);

  wire A_out, ate_out, B_out, fiv_out, four_out, nin_out, not_1_out, not_2_out, not_3_out, not_4_out,
       not_5_out, not_6_out, not_7_out, not_8_out, not_9_out, not_10_out, not_11_out, not_12_out, not_13_out;
  wire [1:0] or_1_out;

  and four (four_out, not_1_out, not_2_out, icode[2], not_3_out);
  not not_1 (not_1_out, icode[0]);
  not not_2 (not_2_out, icode[1]);
  not not_3 (not_3_out, icode[3]);
  or or_1 (or_1_out[0], four_out, fiv_out, ate_out);
  and fiv (fiv_out, icode[0], not_4_out, icode[2], not_5_out);
  not not_4 (not_4_out, icode[1]);
  not not_5 (not_5_out, icode[3]);
  and ate (ate_out, not_6_out, not_7_out, not_8_out, icode[3]);
  not not_6 (not_6_out, icode[0]);
  not not_7 (not_7_out, icode[1]);
  not not_8 (not_8_out, icode[2]);
  and nin (nin_out, icode[0], not_9_out, not_10_out, icode[3]);
  not not_9 (not_9_out, icode[1]);
  or or_2 (or_1_out[1], nin_out, A_out, B_out);
  and A (A_out, not_11_out, icode[1], not_12_out, icode[3]);
  not not_10 (not_10_out, icode[2]);
  not not_11 (not_11_out, icode[0]);
  not not_12 (not_12_out, icode[2]);
  and B (B_out, icode[0], icode[1], not_13_out, icode[3]);
  not not_13 (not_13_out, icode[2]);
  Multiplexer #(.select(2), .width(64)) multiplexer_1 (
    .in1(valE), .in2(valA), .out(Data_memory), .sel(or_1_out));  // open: in0, in3
endmodule

module Mem_data (
  input  [63:0] valA,
  input  [11:0] valP,
  input  [3:0] icode,
  output [63:0] data_mem
);

  wire A_out, eight_out, four_out, not_1_out, not_2_out, not_3_out, not_4_out, not_5_out, not_6_out,
       not_7_out, not_8_out, or_1_out;
  wire [1:0] multiplexer_1_out, multiplexer_2_out, or_2_out;
  wire [63:0] bit_extender_1_out;

  and four (four_out, not_1_out, not_2_out, icode[2], not_3_out);
  not not_1 (not_1_out, icode[0]);
  not not_2 (not_2_out, icode[1]);
  not not_3 (not_3_out, icode[3]);
  not not_4 (not_4_out, icode[0]);
  or or_1 (or_1_out, eight_out, A_out);
  and eight (eight_out, not_4_out, not_5_out, not_6_out, icode[3]);
  not not_5 (not_5_out, icode[1]);
  not not_6 (not_6_out, icode[2]);
  not not_7 (not_7_out, icode[0]);
  Multiplexer #(.width(2)) multiplexer_1 (.in0(2'b00), .in1(2'b01), .out(multiplexer_1_out), .sel(four_out));
  Multiplexer #(.width(2)) multiplexer_2 (.in0(2'b00), .in1(2'b10), .out(multiplexer_2_out), .sel(or_1_out));
  and A (A_out, not_7_out, icode[1], not_8_out, icode[3]);
  not not_8 (not_8_out, icode[2]);
  assign or_2_out = multiplexer_1_out | multiplexer_2_out;  // OR_Gate or_2, 2 bits wide
  Multiplexer #(.select(2), .width(64)) multiplexer_3 (
    .in1(valA), .in2(bit_extender_1_out), .out(data_mem), .sel(or_2_out));  // open: in0, in3
  assign bit_extender_1_out = {{52{valP[11]}}, valP};  // Bit_Extender bit_extender_1
endmodule

module Mem_read (
  input  [3:0] icode,
  input  [4:0] cycle,
  output read
);

  wire and_1_out, and_2_out, and_3_out, multiplexer_1_out, not_1_out, not_2_out, not_3_out, not_4_out,
       not_5_out, or_1_out;

  and and_1 (and_1_out, icode[0], not_1_out, icode[2], not_2_out);
  not not_1 (not_1_out, icode[1]);
  not not_2 (not_2_out, icode[3]);
  and and_2 (and_2_out, icode[0], not_3_out, not_4_out, icode[3]);
  not not_3 (not_3_out, icode[1]);
  not not_4 (not_4_out, icode[2]);
  and and_3 (and_3_out, icode[0], icode[1], not_5_out, icode[3]);
  not not_5 (not_5_out, icode[2]);
  or or_1 (or_1_out, and_1_out, and_2_out, and_3_out);
  and and_4 (read, or_1_out, multiplexer_1_out);
  Multiplexer #(.select(5)) multiplexer_1 (
    .in0(1'b0), .in1(1'b0), .in2(1'b0), .in3(1'b0), .in4(1'b0), .in5(1'b0), .in6(1'b0), .in7(1'b0),
    .in8(1'b0), .in9(1'b1), .in10(1'b1), .in11(1'b1), .in12(1'b1), .in13(1'b1), .in14(1'b1), .in15(1'b1),
    .in16(1'b1), .in17(1'b1), .in18(1'b0), .in19(1'b0), .in20(1'b0), .in21(1'b0), .in22(1'b0), .in23(1'b0),
    .in24(1'b0), .in25(1'b0), .in26(1'b0), .in27(1'b0), .in28(1'b0), .in29(1'b0), .in30(1'b0), .in31(1'b0),
    .out(multiplexer_1_out), .sel(cycle));
endmodule

module Mem_write (
  input  [4:0] cycle,
  input  [3:0] icode,
  output read
);

  wire and_1_out, and_2_out, and_3_out, multiplexer_1_out, not_1_out, not_2_out, not_3_out, not_4_out,
       not_5_out, not_6_out, not_7_out, not_8_out, or_1_out;

  not not_1 (not_1_out, icode[0]);
  not not_2 (not_2_out, icode[1]);
  and and_1 (and_1_out, not_1_out, not_2_out, icode[2], not_3_out);
  not not_3 (not_3_out, icode[3]);
  not not_4 (not_4_out, icode[0]);
  and and_2 (and_2_out, not_4_out, not_5_out, not_6_out, icode[3]);
  not not_5 (not_5_out, icode[1]);
  not not_6 (not_6_out, icode[2]);
  not not_7 (not_7_out, icode[0]);
  or or_1 (or_1_out, and_1_out, and_2_out, and_3_out);
  and and_3 (and_3_out, not_7_out, icode[1], not_8_out, icode[3]);
  not not_8 (not_8_out, icode[2]);
  and and_4 (read, or_1_out, multiplexer_1_out);
  Multiplexer #(.select(5)) multiplexer_1 (
    .in0(1'b0), .in1(1'b0), .in2(1'b0), .in3(1'b0), .in4(1'b0), .in5(1'b0), .in6(1'b0), .in7(1'b0),
    .in8(1'b0), .in9(1'b0), .in10(1'b1), .in11(1'b1), .in12(1'b1), .in13(1'b1), .in14(1'b1), .in15(1'b1),
    .in16(1'b1), .in17(1'b1), .in18(1'b1), .in19(1'b0), .in20(1'b0), .in21(1'b0), .in22(1'b0), .in23(1'b0),
    .in24(1'b0), .in25(1'b0), .in26(1'b0), .in27(1'b0), .in28(1'b0), .in29(1'b0), .in30(1'b0), .in31(1'b0),
    .out(multiplexer_1_out), .sel(cycle));
endmodule

module Data_memory (
  input  [63:0] memaddr,
  input  clk,
  input  write,
  input  read,
  input  [63:0] memdata,
  input  [4:0] cycle_num,
  output [63:0] valM
);

  wire demultiplexer_2_out10, demultiplexer_2_out11, demultiplexer_2_out12, demultiplexer_2_out13,
       demultiplexer_2_out14, demultiplexer_2_out15, demultiplexer_2_out16, demultiplexer_2_out17,
       subtractor_1_bout;
  wire [4:0] subtractor_1_out;
  wire [7:0] demultiplexer_1_out10, demultiplexer_1_out11, demultiplexer_1_out12, demultiplexer_1_out13,
       demultiplexer_1_out14, demultiplexer_1_out15, demultiplexer_1_out16, demultiplexer_1_out17,
       multiplexer_2_out, ram_1_dout;
  wire [11:0] adder_1_out, bit_extender_1_out, multiplexer_1_out;

  assign bit_extender_1_out = {{7{subtractor_1_out[4]}}, subtractor_1_out};  // Bit_Extender bit_extender_1
  Subtractor #(.width(5)) subtractor_1 (
    .a(cycle_num), .b(5'b01011), .out(subtractor_1_out), .bout(subtractor_1_bout));  // open: bin
  Multiplexer #(.width(12)) multiplexer_1 (
    .in0(bit_extender_1_out), .in1({12{1'b0}}), .out(multiplexer_1_out), .sel(subtractor_1_bout));
  Adder #(.width(12)) adder_1 (.a(memaddr[11:0]), .b(multiplexer_1_out), .out(adder_1_out));  // open: cin, cout
  RAM #(.addrWidth(12)) ram_1 (
    .addr(adder_1_out), .we(write), .oe(read), .clk(clk), .din(multiplexer_2_out), .dout(ram_1_dout));
  Multiplexer #(.select(5), .width(8)) multiplexer_2 (
    .in11(memdata[7:0]), .in12(memdata[15:8]), .in13(memdata[23:16]), .in14(memdata[31:24]),
    .in15(memdata[39:32]), .in16(memdata[47:40]), .in17(memdata[55:48]), .in18(memdata[63:56]),
    .out(multiplexer_2_out), .sel(cycle_num));  // open: in0, in1, in2, in3, in4, in5, in6, in7, in8, in9, in10, in19, in20, in21, in22, in23, in24, in25, in26, in27, in28, in29, in30, in31
  Demultiplexer #(.select(5), .width(8)) demultiplexer_1 (
    .out10(demultiplexer_1_out10), .out11(demultiplexer_1_out11), .out12(demultiplexer_1_out12),
    .out13(demultiplexer_1_out13), .out14(demultiplexer_1_out14), .out15(demultiplexer_1_out15),
    .out16(demultiplexer_1_out16), .out17(demultiplexer_1_out17), .in(ram_1_dout), .sel(cycle_num));  // open: out0, out1, out2, out3, out4, out5, out6, out7, out8, out9, out18, out19, out20, out21, out22, out23, out24, out25, out26, out27, out28, out29, out30, out31
  Demultiplexer #(.select(5)) demultiplexer_2 (
    .out10(demultiplexer_2_out10), .out11(demultiplexer_2_out11), .out12(demultiplexer_2_out12),
    .out13(demultiplexer_2_out13), .out14(demultiplexer_2_out14), .out15(demultiplexer_2_out15),
    .out16(demultiplexer_2_out16), .out17(demultiplexer_2_out17), .in(read), .sel(cycle_num));  // open: out0, out1, out2, out3, out4, out5, out6, out7, out8, out9, out18, out19, out20, out21, out22, out23, out24, out25, out26, out27, out28, out29, out30, out31
  Register register_1 (.D(demultiplexer_1_out10), .en(demultiplexer_2_out10), .Q(valM[7:0]), .clk(clk));  // open: clr
  Register register_2 (.D(demultiplexer_1_out11), .en(demultiplexer_2_out11), .Q(valM[15:8]), .clk(clk));  // open: clr
  Register register_3 (.D(demultiplexer_1_out12), .en(demultiplexer_2_out12), .Q(valM[23:16]), .clk(clk));  // open: clr
  Register register_4 (.D(demultiplexer_1_out13), .en(demultiplexer_2_out13), .Q(valM[31:24]), .clk(clk));  // open: clr
  Register register_5 (.D(demultiplexer_1_out14), .en(demultiplexer_2_out14), .Q(valM[39:32]), .clk(clk));  // open: clr
  Register register_6 (.D(demultiplexer_1_out15), .en(demultiplexer_2_out15), .Q(valM[47:40]), .clk(clk));  // open: clr
  Register register_7 (.D(demultiplexer_1_out16), .en(demultiplexer_2_out16), .Q(valM[55:48]), .clk(clk));  // open: clr
  Register register_8 (.D(demultiplexer_1_out17), .en(demultiplexer_2_out17), .Q(valM[63:56]), .clk(clk));  // open: clr
endmodule

module fetch (
  input  [11:0] PC,
  input  clk,
  output [3:0] icode,
  output [3:0] ifun,
  output [4:0] count,
  output [3:0] rA,
  output [3:0] rB,
  output [63:0] valC,
  output [11:0] valP
);

  wire multiplexer_2_out;
  wire [7:0] read_1_byte_1, read_1_byte_2, read_1_byte_3, read_1_byte_4, read_1_byte_5, read_1_byte_6,
       read_1_byte_7, read_1_byte_8, read_1_byte_9, rom_1_data;
  wire [11:0] cyclecount_1_address_out, multiplexer_1_out, register_1_q;

  ROM #(.addrWidth(12)) rom_1 (.addr(cyclecount_1_address_out), .data(rom_1_data));
  Register #(.width(12)) register_1 (.D(PC), .clk(clk), .Q(register_1_q));  // open: en, clr
  CycleCount cyclecount_1 (
    .address_in(register_1_q), .clk(clk), .address_out(cyclecount_1_address_out), .count_out(count));
  read read_1 (
    .ReadByte(rom_1_data), .cycle_count(count), .clock(clk), .byte_0({ifun, icode}), .byte_1(read_1_byte_1),
    .byte_2(read_1_byte_2), .byte_3(read_1_byte_3), .byte_4(read_1_byte_4), .byte_5(read_1_byte_5),
    .byte_6(read_1_byte_6), .byte_7(read_1_byte_7), .byte_8(read_1_byte_8), .byte_9(read_1_byte_9));
  Multiplexer #(.select(4), .width(12)) multiplexer_1 (
    .in0(12'h1), .in1(12'h1), .in2(12'h2), .in3(12'ha), .in4(12'ha), .in5(12'ha), .in6(12'h2), .in7(12'h9),
    .in8(12'h9), .in9(12'h1), .in10(12'h2), .in11(12'h2), .out(multiplexer_1_out), .sel(icode));  // open: in12, in13, in14, in15
  Multiplexer #(.select(4)) multiplexer_2 (
    .in0(1'b0), .in1(1'b1), .in2(1'b1), .in3(1'b1), .in4(1'b1), .in5(1'b1), .in6(1'b0), .in7(1'b0),
    .in8(1'b0), .in9(1'b1), .in10(1'b1), .in11(1'b0), .in12(1'b0), .in13(1'b0), .in14(1'b0), .in15(1'b0),
    .out(multiplexer_2_out), .sel(icode));
  Align align_1 (
    .NeedRegis(multiplexer_2_out), .B1(read_1_byte_1), .B2(read_1_byte_2), .B3(read_1_byte_3),
    .B4(read_1_byte_4), .B5(read_1_byte_5), .B6(read_1_byte_6), .B7(read_1_byte_7), .B8(read_1_byte_8),
    .B9(read_1_byte_9), .rA(rA), .rB(rB), .Valc(valC));
  Adder #(.width(12)) adder_1 (.a(multiplexer_1_out), .b(register_1_q), .out(valP));  // open: cin, cout

  // Notes on the sheet:
  //   contents of rom_1 (hex, n*v repeats v):
  //   45 3a 78 1 13 45 78 43 67 89 23 45 67 89 6
endmodule

module cycle_count (
  input  clk,
  output [4:0] count
);

  Counter #(.max('h13), .width(5)) counter_1 (.clk(clk), .Q(count));  // open: clr, load, up, count, D, carry
endmodule

module address (
  input  [11:0] PC,
  input  [4:0] cycle,
  output [11:0] addr
);

  wire [11:0] multiplexer_1_out;

  Multiplexer #(.select(5), .width(12)) multiplexer_1 (
    .in0({12{1'b0}}), .in1(12'h1), .in2(12'h2), .in3(12'h3), .in4(12'h4), .in5(12'h5), .in6(12'h6),
    .in7(12'h7), .in8(12'h8), .in9(12'h9), .in10({12{1'b0}}), .in11({12{1'b0}}), .in12({12{1'b0}}),
    .in13({12{1'b0}}), .in14({12{1'b0}}), .in15({12{1'b0}}), .in16({12{1'b0}}), .in17({12{1'b0}}),
    .in18({12{1'b0}}), .in19({12{1'b0}}), .out(multiplexer_1_out), .sel(cycle));  // open: in20, in21, in22, in23, in24, in25, in26, in27, in28, in29, in30, in31
  Adder #(.width(12)) adder_1 (.a(multiplexer_1_out), .b(PC), .out(addr));  // open: cin, cout
endmodule

module PC (
);

  wire [4:0] undriven_2;
  wire [11:0] address_1_addr, register_1_q, undriven;

  Register #(.width(12)) register_1 (.D(undriven), .en(1'b1), .Q(register_1_q));  // open: clk, clr
  address address_1 (.cycle(undriven_2), .PC(register_1_q), .addr(address_1_addr));
  ROM #(.addrWidth(12)) rom_1 (.addr(address_1_addr));  // open: data
endmodule
